# Fritzing sketch esp32 s3 2 factor authentication project (saved by Fritzing 0.8.7b)

parts:
  M1 = ESP32-S2-DevKitC-1 [part_number=ESP32-S2-DevKitC-1]
  Matrix_keypad1 = KEYPAD 4x4
  LED1 = LED - 3mm [color="Red (633nm)" package="3 mm [THT]"]
  J1 = Piezo Speaker

nets:
  N1: M1.pin_5, LED1.anode
  N2: M1.pin_8, Matrix_keypad1.row4
  N3: M1.pin_9, Matrix_keypad1.col4
  N4: M1.pin_10, Matrix_keypad1.col3
  N5: M1.pin_11, Matrix_keypad1.col2
  N6: M1.pin_18, Matrix_keypad1.row1
  N7: M1.pin_19, Matrix_keypad1.row2
  N8: M1.pin_20, Matrix_keypad1.row3
  N9: M1.pin_22, M1.pin_44, LED1.cathode, J1.pin1
  N10: M1.pin_27, Matrix_keypad1.col1

custom parts:
  ESP32-S2-DevKitC-1: ESP32-S2-DevKitC-1 is an entry-level development board based on ESP32-S2-SOLO (on-board PCB antenna). It is based on the ESP32 microcontroller that boasts Wifi, Bluetooth, Ethernet and Low Power support all in a single chip. (vanepp) Feb 2022: converted to ESP32-S2-DevKitC-1. This module is 44pins long (2x22) and 11 pins width.
  KEYPAD 4x4: Matrix keypad 16 buttons, 4 rows x 4 columns
