# Fritzing sketch shutter (saved by Fritzing 0.8.7b)
breadboards: 1

parts:
  IC1 = L293D [package=THT]
  Part1 = Arduino Nano (Rev3.0)
  U1 = Mini-360 DC-DC Buck converter [package=THT]
  DC_Mot_Enc1 = DC Motor with two-phase hall-encoder [part_number=VT-E-G25A-06-177E]

nets:
  N1: IC1.In_1, Part1.D5
  N2: IC1.Out_1_(_Controlled_by_Enable_1_), DC_Mot_Enc1.pin2
  N3: IC1.0V, Part1.GND, U1.OUT-
  N4: IC1.Out_2_(_Controlled_by_Enable_1_), DC_Mot_Enc1.pin1
  N5: IC1.In_2, Part1.D4
  N6: IC1.+V, Part1.5V

notes:
  Boost convertor 5 volt
  3 volts for motor

custom parts:
  Mini-360 DC-DC Buck converter: Mini-360 DC-DC Buck converter. Tiny buck step down voltage converter, input voltage 4.75 to 23V output 1 to 17V adjustable. Available from ebay and the like.
