# Fritzing sketch esp32_firebeetle_mlx90614_schmatic (saved by Fritzing 0.8.7b)

parts:
  M1 = FireBeetle ESP32-E
  U2 = MLX90614 [package=to-39]

nets:
  N1: M1.pin_10, M1.pin_26, U2.PWM_SDA
  N2: M1.pin_11, M1.pin_25, U2.SCL_VZ
  N3: M1.pin_12, U2.VSS
  N4: M1.pin_18, U2.VDD

notes:
  Battery
  +VE -VE
  Battery Measurement done inter nally on pin A2/IO34
  MLX90614
  Input Voltage: 3.3V-5.5V

custom parts:
  FireBeetle ESP32-E: FireBeetle ESP32-E, specially designed for IoT, is an ESP-WROOM-32E-based main controller board with dual-core chips. It supports WiFi and Bluetooth dual-mode communication and features a small size, ultra-low power consumption, on-board charging circuit, and easy-to-use interface, which can be conveniently used for smart home IoT, industrial IoT applications, wearable devices, and so on. You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
