# Fritzing sketch schematic (saved by Fritzing 0.8.7b)
breadboards: 1

parts:
  U5 = ESP32-38PinWide [part_number=ESP32-38PinWide]
  Part1 = 12 NeoPixel Ring [part_number=1643]
  SIM800L_BO2 = SIM800L BO
  GY2 = MPU-6050 Board GY-521 [form="♀ (female)" package=THT]
  ANT2 = Antenna
  VCC3 = 4 x AAA Battery Mount
  R1 = Resistor [tolerance=±5% resistance=220 package=THT]
  R2 = Resistor [tolerance=±5% resistance=220 package=THT]
  U6 = Mini-360 DC-DC Buck converter [package=THT]

nets:
  N1: U5.3.3, GY2.pin1
  N2: U5.GPIO12, SIM800L_BO2.pin_4
  N3: U5.GND, GY2.pin2
  N4: U5.GPIO13, SIM800L_BO2.pin_5
  N5: U5.VIN, U6.OUT+
  N6: U5.GPIO21, GY2.pin4
  N7: U5.GPIO3, Part1.IN
  N8: U5.GPIO22, GY2.pin3
  N9: SIM800L_BO2.PIN1, ANT2.antenna_lead
  N10: SIM800L_BO2.PIN2, VCC3.+, R1.Pin_0
  N11: VCC3.-, R2.Pin_0

notes:
  + 3.3 volts coming from here for battery voltage going to pin 4
  DC 4.2 volts source
  2.7k ohms
  10k ohms
  boost convertor for +5 volts for ring and esp

custom parts:
  ESP32-38PinWide: Generic 38-Pin ESP32 with wide format (only access to one side of pins on a breadboard) based on Stephen Lilley's HiLetgo ESP-WROOM-32 ESP32 ESP-32S Development Board.
  12 NeoPixel Ring: 12 ultra bright smart LED NeoPixels are arranged in a circle with 1.5" (37mm) outer diameter. The rings are 'chainable' - connect the output pin of one to the input pin of another. Use only one microcontroller pin to control as many as you can chain together! Each LED is addressable as the driver chip is inside the LED. Each one has ~18mA constant current drive so the color will be very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
  MPU-6050 Board GY-521: Acelerometro y Giroscopio MPU-6050 Board GY-521
  Mini-360 DC-DC Buck converter: Mini-360 DC-DC Buck converter. Tiny buck step down voltage converter, input voltage 4.75 to 23V output 1 to 17V adjustable. Available from ebay and the like.
