# Fritzing sketch AudioGuestbook (saved by Fritzing 0.8.7b)

parts:
  J4 = female pin header, 2 pins [form="♀ (female)"]
  J6 = female pin header, 2 pins [form="♀ (female)"]
  J11 = female pin header, 2 pins [form="♀ (female)"]  # not connected
  J12 = male pin header, 2 pins [form="♂ (male)"]
  J14 = female pin header, 10 pins [form="♀ (female)"]  # not connected
  J15 = female pin header, 10 pins [form="♀ (female)"]

nets:
  N1: J4.pin1, J15.pin9
  N2: J4.pin2, J15.pin10
  N3: J6.pin1, J12.pin2
  N4: J6.pin2, J12.pin1

notes:
  Speaker
  +ve (white) -> 3.5mm tip
  -ve (blue) -> 3.5mm sleeve
  Hook switch
  (black) -> GND
  (white) -> Teensy Pin 0
  Microphone
  +ve (red) -> Teensy Mic
  -ve (green) -> GND
  Telephone, e.g. GPO746
  Teensy 4.0 with Audio Shield
